// Logisim project CPU (1).circ as structural Verilog
module main (
  input  in_1,
  output [7:0] A_Bus,
  output [7:0] B_Bus,
  output [3:0] B,
  output [3:0] A,
  output [3:0] OpCode,
  output [7:0] Data,
  output [3:0] Dest,
  output [7:0] C_Bus
);

  wire CLK, comparator_1_lt, comparator_2_lt, counter_1_carry, enable, not_1_out, Reset, TClock;
  wire [3:0] rom_1_data;
  wire [4:0] counter_1_q, n5_bit_pc_1_output;
  wire [6:0] adder_1_out, adder_2_out, LSB, MSB;
  wire [7:0] multiplexer_3_out, R0, R1, R2, R3, R4, R5, R6, R7, R8;
  wire [8:0] decoder_1_out0;

  _5_bit_PC u_5_bit_pc_1 (.CLK(in_1), ._0(CLK), .\output (n5_bit_pc_1_output));
  RAM #(.addrWidth(5), .dataWidth(24)) ram_1 (
    .addr(n5_bit_pc_1_output), .data({OpCode, Dest, A, B, Data}), .clk(CLK));  // open: sel, ld, clr
  Decoder #(.select(4)) decoder_1 (
    .out0(decoder_1_out0[0]), .out1(decoder_1_out0[1]), .out2(decoder_1_out0[2]), .out3(decoder_1_out0[3]),
    .out4(decoder_1_out0[4]), .out5(decoder_1_out0[5]), .out6(decoder_1_out0[6]), .out7(decoder_1_out0[7]),
    .out8(decoder_1_out0[8]), .sel(Dest), .en(enable));  // open: out9, out10, out11, out12, out13, out14, out15
  Multiplexer #(.select(4), .width(8)) multiplexer_1 (
    .in0(R0), .in1(R1), .in2(R2), .in3(R3), .in4(R4), .in5(R5), .in6(R6), .in7(R7), .in8(R8), .out(A_Bus),
    .sel(A));  // open: in9, in10, in11, in12, in13, in14, in15, en
  Multiplexer #(.select(4), .width(8)) multiplexer_2 (
    .in0(R0), .in1(R1), .in2(R2), .in3(R3), .in4(R4), .in5(R5), .in6(R6), .in7(R7), .in8(R8), .in9(Data),
    .out(B_Bus), .sel(B));  // open: in10, in11, in12, in13, in14, in15, en
  _8_bit_ALU u_8_bit_alu_1 (.B(B_Bus), .A(A_Bus), .Opcode(OpCode), .Output(C_Bus));  // open: Zero_Flag
  Register_Bank ReBank (
    .CLK(CLK), .enable(C_Bus), ._7_bit_one_hot(decoder_1_out0), .R0(R0), .R1(R1), .R2(R2), .R3(R3), .R4(R4),
    .R5(R5), .R6(R6), .R7(R7), .R8(R8));
  TTY #(.rows(33), .cols(1)) tty_1 (.data(MSB), .clk(TClock), .clr(Reset));  // open: we
  TTY #(.rows(33), .cols(1)) tty_2 (.data(LSB), .clk(TClock), .clr(Reset));  // open: we
  Button u_Reset (.out(Reset));
  Counter #(.width(5), .max('h1f)) counter_1 (
    .Q(counter_1_q), .carry(counter_1_carry), .clk(TClock), .clr(Reset));  // open: load, D, count
  Multiplexer #(.select(4), .width(8), .disabled(0), .enable("false")) multiplexer_3 (
    .in0(R0), .in1(R1), .in2(R2), .in3(R3), .in4(R4), .in5(R5), .in6(R6), .in7(R7), .in8(R8),
    .out(multiplexer_3_out), .sel(rom_1_data));  // open: in9, in10, in11, in12, in13, in14, in15
  not not_1 (not_1_out, counter_1_carry);
  Clock clock_1 (.out(CLK));
  and and_1 (TClock, not_1_out, CLK);
  Comparator #(.width(7)) comparator_1 (
    .a(7'b0111001), .b({3'b011, multiplexer_3_out[3:0]}), .lt(comparator_1_lt));  // open: gt, eq
  Comparator #(.width(7)) comparator_2 (
    .a(7'b0111001), .b({3'b011, multiplexer_3_out[7:4]}), .lt(comparator_2_lt));  // open: gt, eq
  ROM #(.addrWidth(5), .dataWidth(4)) rom_1 (.addr(counter_1_q), .data(rom_1_data));  // open: sel
  Adder #(.width(7)) adder_1 (
    .a({3'b011, multiplexer_3_out[3:0]}), .b(7'b0000111), .out(adder_1_out));  // open: cin, cout
  Adder #(.width(7)) adder_2 (
    .a({3'b011, multiplexer_3_out[7:4]}), .b(7'b0000111), .out(adder_2_out));  // open: cin, cout
  Multiplexer #(.width(7), .disabled(0), .enable("false")) multiplexer_4 (
    .in0({3'b011, multiplexer_3_out[3:0]}), .in1(adder_1_out), .out(LSB), .sel(comparator_1_lt));
  Multiplexer #(.width(7), .disabled(0), .enable("false")) multiplexer_5 (
    .in0({3'b011, multiplexer_3_out[7:4]}), .in1(adder_2_out), .out(MSB), .sel(comparator_2_lt));

  // Notes on the sheet:
  //   00
  //   F5
  //   5A
  //   50
  //   FF
  //   0A
  //   4F
  //   F5
  //   EA
  //   7A
  //   9B
  //   65
  //   0F
  //   FF
  //   F5
  //   AA
  //   5A
  //   0A
  //   FA
  //   A5
  //   04
  //   5A
  //   B4
  //   2D
  //   0A
  //   B0
  //   50
  //   0F
  //   00
  //   00
  //   5A
  //   contents of rom_1 (hex, n*v repeats v):
  //   0 0 1 2 3 4 5 6 7 8 2 3 4 5 0 0 1 6 7 8 2 3 4 5 6 6 7 8 2 3 4 4
endmodule

module _8_bit_ALU (
  input  [3:0] Opcode,
  input  [7:0] Output,
  input  [7:0] A,
  input  [7:0] B,
  input  Zero_Flag
);

  wire _0_cout_minus, _0_cout_plus, _1_cout_minus, _1_cout_plus, _2_cout_minus, _2_cout_plus, _3_cout_minus,
       _3_cout_plus, _4_cout_minus, _4_cout_plus, _5_cout_minus, _5_cout_plus, _6_cout_minus, _6_cout_plus;

  _1bit_ALU _0 (
    .opcode(Opcode), .bit1(A[0]), .bit2(B[0]), .OUTPUT(Output[7]), .C_IN_plus(1'b0), .next(A[1]),
    .previous(1'b0), .COUT_plus(_0_cout_plus), .CIN_minus(1'b1), .COUT_minus(_0_cout_minus));  // open: HALT
  _1bit_ALU _1 (
    .opcode(Opcode), .bit1(A[1]), .bit2(B[1]), .OUTPUT(Output[6]), .C_IN_plus(_0_cout_plus), .next(A[2]),
    .previous(A[0]), .COUT_plus(_1_cout_plus), .CIN_minus(_0_cout_minus), .COUT_minus(_1_cout_minus));  // open: HALT
  _1bit_ALU _2 (
    .opcode(Opcode), .bit1(A[2]), .bit2(B[2]), .OUTPUT(Output[5]), .C_IN_plus(_1_cout_plus), .next(A[3]),
    .previous(A[1]), .COUT_plus(_2_cout_plus), .CIN_minus(_1_cout_minus), .COUT_minus(_2_cout_minus));  // open: HALT
  _1bit_ALU _3 (
    .opcode(Opcode), .bit1(A[3]), .bit2(B[3]), .OUTPUT(Output[4]), .C_IN_plus(_2_cout_plus), .next(A[4]),
    .previous(A[2]), .COUT_plus(_3_cout_plus), .CIN_minus(_2_cout_minus), .COUT_minus(_3_cout_minus));  // open: HALT
  _1bit_ALU _4 (
    .opcode(Opcode), .bit1(A[4]), .bit2(B[4]), .OUTPUT(Output[3]), .C_IN_plus(_3_cout_plus), .next(A[5]),
    .previous(A[3]), .COUT_plus(_4_cout_plus), .CIN_minus(_3_cout_minus), .COUT_minus(_4_cout_minus));  // open: HALT
  _1bit_ALU _5 (
    .opcode(Opcode), .bit1(A[5]), .bit2(B[5]), .OUTPUT(Output[2]), .C_IN_plus(_4_cout_plus), .next(A[6]),
    .previous(A[4]), .COUT_plus(_5_cout_plus), .CIN_minus(_4_cout_minus), .COUT_minus(_5_cout_minus));  // open: HALT
  _1bit_ALU _6 (
    .opcode(Opcode), .bit1(A[6]), .bit2(B[6]), .OUTPUT(Output[1]), .C_IN_plus(_5_cout_plus), .next(A[7]),
    .previous(A[5]), .COUT_plus(_6_cout_plus), .CIN_minus(_5_cout_minus), .COUT_minus(_6_cout_minus));  // open: HALT
  _1bit_ALU _7 (
    .opcode(Opcode), .bit1(A[7]), .bit2(B[7]), .OUTPUT(Output[0]), .C_IN_plus(_6_cout_plus), .next(1'b0),
    .previous(A[6]), .CIN_minus(_6_cout_minus));  // open: HALT, COUT_plus, COUT_minus
  nor nor_1 (Zero_Flag, Output[7], Output[6], Output[5], Output[4], Output[3], Output[2], Output[1], Output[0]);
endmodule

module Register_Bank (
  input  CLK,
  input  [7:0] enable,
  input  [8:0] _7_bit_one_hot,
  output [7:0] R0,
  output [7:0] R1,
  output [7:0] R2,
  output [7:0] R3,
  output [7:0] R4,
  output [7:0] R5,
  output [7:0] R6,
  output [7:0] R7,
  output [7:0] R8
);

  _8_bit_Reg u_8_bit_reg_1 (.Enable(_7_bit_one_hot[0]), .CLK(CLK), ._8_bit_input(enable), .\output (R0));
  _8_bit_Reg u_8_bit_reg_2 (.Enable(_7_bit_one_hot[1]), .CLK(CLK), ._8_bit_input(enable), .\output (R1));
  _8_bit_Reg u_8_bit_reg_3 (.Enable(_7_bit_one_hot[2]), .CLK(CLK), ._8_bit_input(enable), .\output (R2));
  _8_bit_Reg u_8_bit_reg_4 (.Enable(_7_bit_one_hot[3]), .CLK(CLK), ._8_bit_input(enable), .\output (R3));
  _8_bit_Reg u_8_bit_reg_5 (.Enable(_7_bit_one_hot[4]), .CLK(CLK), ._8_bit_input(enable), .\output (R4));
  _8_bit_Reg u_8_bit_reg_6 (.Enable(_7_bit_one_hot[5]), .CLK(CLK), ._8_bit_input(enable), .\output (R5));
  _8_bit_Reg u_8_bit_reg_7 (.Enable(_7_bit_one_hot[6]), .CLK(CLK), ._8_bit_input(enable), .\output (R6));
  _8_bit_Reg u_8_bit_reg_8 (.Enable(_7_bit_one_hot[7]), .CLK(CLK), ._8_bit_input(enable), .\output (R7));
  _8_bit_Reg u_8_bit_reg_9 (.Enable(_7_bit_one_hot[8]), .CLK(CLK), ._8_bit_input(enable), .\output (R8));
endmodule

module _5_bit_Pc (
  input  enable,
  input  CLK,
  input  [4:0] _5bitPC,
  output [4:0] \output 
);

  D_Flip_Flop d_ff_1 (.clk(CLK), .D(_5bitPC[0]), .Q(\output [0]), .en(enable));  // open: Qn, preset, reset
  D_Flip_Flop d_ff_2 (.clk(CLK), .D(_5bitPC[1]), .Q(\output [1]), .en(enable));  // open: Qn, preset, reset
  D_Flip_Flop d_ff_3 (.clk(CLK), .D(_5bitPC[2]), .Q(\output [2]), .en(enable));  // open: Qn, preset, reset
  D_Flip_Flop d_ff_4 (.clk(CLK), .D(_5bitPC[3]), .Q(\output [3]), .en(enable));  // open: Qn, preset, reset
  D_Flip_Flop d_ff_5 (.clk(CLK), .D(_5bitPC[4]), .Q(\output [4]), .en(enable));  // open: Qn, preset, reset
endmodule

module _8_bit_Reg (
  input  Enable,
  input  CLK,
  input  [7:0] _8_bit_input,
  output [7:0] \output 
);

  D_Flip_Flop d_ff_1 (.clk(CLK), .D(_8_bit_input[0]), .Q(\output [0]), .en(Enable));  // open: Qn, preset, reset
  D_Flip_Flop d_ff_2 (.clk(CLK), .D(_8_bit_input[1]), .Q(\output [1]), .en(Enable));  // open: Qn, preset, reset
  D_Flip_Flop d_ff_3 (.clk(CLK), .D(_8_bit_input[2]), .Q(\output [2]), .en(Enable));  // open: Qn, preset, reset
  D_Flip_Flop d_ff_4 (.clk(CLK), .D(_8_bit_input[3]), .Q(\output [3]), .en(Enable));  // open: Qn, preset, reset
  D_Flip_Flop d_ff_5 (.clk(CLK), .D(_8_bit_input[4]), .Q(\output [4]), .en(Enable));  // open: Qn, preset, reset
  D_Flip_Flop d_ff_6 (.clk(CLK), .D(_8_bit_input[5]), .Q(\output [5]), .en(Enable));  // open: Qn, preset, reset
  D_Flip_Flop d_ff_7 (.clk(CLK), .D(_8_bit_input[6]), .Q(\output [6]), .en(Enable));  // open: Qn, preset, reset
  D_Flip_Flop d_ff_8 (.clk(CLK), .D(_8_bit_input[7]), .Q(\output [7]), .en(Enable));  // open: Qn, preset, reset
endmodule

module _1bit_ALU (
  input  [3:0] opcode,
  input  bit1,
  input  bit2,
  input  C_IN_plus,
  input  HALT,
  input  next,
  input  previous,
  input  CIN_minus,
  output OUTPUT,
  output COUT_plus,
  output COUT_minus
);

  wire adder_1_s, adder_2_s, AND_out, not_1_out, not_2_out, OR_out;

  not not_1 (not_1_out, bit1);
  not not_2 (not_2_out, bit2);
  and AND (AND_out, bit1, bit2);
  or OR (OR_out, bit1, bit2);
  adder adder_1 (.bit1(bit1), .bit2(bit2), .c(C_IN_plus), .s(adder_1_s), .cout(COUT_plus));
  adder adder_2 (.bit1(bit1), .bit2(not_2_out), .c(CIN_minus), .s(adder_2_s), .cout(COUT_minus));
  Multiplexer #(.select(4), .enable("false")) multiplexer_1 (
    .in0(AND_out), .in1(OR_out), .in2(not_1_out), .in3(adder_1_s), .in4(bit1), .in5(next), .in6(previous),
    .in7(adder_2_s), .in8(adder_1_s), .in9(adder_2_s), .in10(bit2), .in11(OUTPUT), .in12(HALT), .out(OUTPUT),
    .sel(opcode));  // open: in13, in14, in15

  // Notes on the sheet:
  //   ADD/SUB
endmodule

module _5_bit_PC (
  input  CLK,
  input  _0,
  output [4:0] \output 
);

  wire not_1_out, t_ff_1_qn, t_ff_2_qn, t_ff_3_qn, t_ff_4_qn;

  not not_1 (not_1_out, _0);
  T_Flip_Flop t_ff_1 (.clk(CLK), .T(not_1_out), .Q(\output [0]), .Qn(t_ff_1_qn));  // open: preset, reset, en
  T_Flip_Flop t_ff_2 (.clk(t_ff_1_qn), .T(not_1_out), .Q(\output [1]), .Qn(t_ff_2_qn));  // open: preset, reset, en
  T_Flip_Flop t_ff_3 (.clk(t_ff_2_qn), .T(not_1_out), .Q(\output [2]), .Qn(t_ff_3_qn));  // open: preset, reset, en
  T_Flip_Flop t_ff_4 (.clk(t_ff_3_qn), .T(not_1_out), .Q(\output [3]), .Qn(t_ff_4_qn));  // open: preset, reset, en
  T_Flip_Flop t_ff_5 (.clk(t_ff_4_qn), .T(not_1_out), .Q(\output [4]));  // open: Qn, preset, reset, en
endmodule

module adder (
  input  bit1,
  input  bit2,
  input  c,
  output s,
  output cout
);

  wire and_1_out, and_2_out, xor_1_out;

  xor xor_1 (xor_1_out, bit1, bit2);
  and and_1 (and_1_out, bit2, bit1);
  and and_2 (and_2_out, xor_1_out, c);
  xor xor_2 (s, xor_1_out, c);
  or or_1 (cout, and_2_out, and_1_out);
endmodule

module _4_bit_ALU_Label (
);

  wire A0, A1, A2, A3, and_1_out, B0, B1, B2, B3, C0, C1, C2, C3, C4, Ca1, Ca2, Ca3, Ca4, CIN, CinP0_out,
       CinP0P1_out, CinP0P1P2_out, G0, G1, G2, G3, not_1_out, not_2_out, not_3_out, not_4_out, P0, P1,
       P1G0_out, P2, P2G1_out, P2P1G0_out, P3, P3G2_out, P3P2G1_out, P3P2P1G0_out, P3P2P1P0Cin_out, S0, S1,
       xor_1_out, xor_2_out, xor_3_out, xor_4_out, xor_5_out, xor_6_out, xor_7_out, xor_8_out;

  and A0B0 (G0, A0, B0);
  or or_1 (P0, A0, B0);
  not not_1 (not_1_out, A0);
  xor xor_1 (xor_1_out, B0, A0);
  and A1B1 (G1, A1, B1);
  or or_2 (P1, A1, B1);
  not not_2 (not_2_out, A1);
  xor xor_2 (xor_2_out, B1, A1);
  and A2B2 (G2, A2, B2);
  or or_3 (P2, A2, B2);
  not not_3 (not_3_out, A2);
  xor xor_3 (xor_3_out, B2, A2);
  and A3B3 (G3, A3, B3);
  or or_4 (P3, A3, B3);
  not not_4 (not_4_out, A3);
  xor xor_4 (xor_4_out, B3, A3);
  xor xor_5 (xor_5_out, xor_1_out, CIN);
  xor xor_6 (xor_6_out, xor_2_out, Ca1);
  xor xor_7 (xor_7_out, xor_3_out, Ca2);
  xor xor_8 (xor_8_out, xor_4_out, Ca3);
  and and_1 (and_1_out, xor_4_out, Ca3);
  Multiplexer #(.select(2), .enable("false")) multiplexer_1 (
    .in0(G0), .in1(P0), .in2(not_1_out), .in3(xor_5_out), .out(C0), .sel({S1, S0}));
  Multiplexer #(.select(2), .enable("false")) multiplexer_2 (
    .in0(G1), .in1(P1), .in2(not_2_out), .in3(xor_6_out), .out(C1), .sel({S1, S0}));
  Multiplexer #(.select(2), .enable("false")) multiplexer_3 (
    .in0(G2), .in1(P2), .in2(not_3_out), .in3(xor_7_out), .out(C2), .sel({S1, S0}));
  Multiplexer #(.select(2), .enable("false")) multiplexer_4 (
    .in0(G3), .in1(P3), .in2(not_4_out), .in3(xor_8_out), .out(C3), .sel({S1, S0}));
  or or_5 (C4, and_1_out, G3);
  and CinP0 (CinP0_out, P0, CIN);
  and CinP0P1 (CinP0P1_out, P0, CIN, P1);
  and P1G0 (P1G0_out, G0, P1);
  and CinP0P1P2 (CinP0P1P2_out, CIN, P0, P1, P2);
  and P2P1G0 (P2P1G0_out, P2, P1, G0);
  and P2G1 (P2G1_out, P2, G1);
  and P3G2 (P3G2_out, P3, G2);
  and P3P2G1 (P3P2G1_out, P3, P2, G1);
  and P3P2P1G0 (P3P2P1G0_out, P3, P2, P1, G0);
  and P3P2P1P0Cin (P3P2P1P0Cin_out, P3, P2, P1, P0, CIN);
  or or_6 (Ca1, CinP0_out, G0);
  or or_7 (Ca2, CinP0P1_out, P1G0_out, G1);
  or or_8 (Ca3, CinP0P1P2_out, P2P1G0_out, P2G1_out, G2);
  or or_9 (Ca4, P3G2_out, P3P2G1_out, P3P2P1G0_out, P3P2P1P0Cin_out, G3);
endmodule

module _4_bit_ALU (
  input  G0,
  input  P3,
  input  G3,
  input  P0,
  input  P1,
  input  P2,
  input  G0_2,
  input  G1,
  input  G2,
  input  CIN,
  input  P0_2,
  input  A0,
  input  B0,
  input  CIN_2,
  input  G1_2,
  input  P1_2,
  input  A1,
  input  B1,
  input  Ca1,
  input  G2_2,
  input  P2_2,
  input  A2,
  input  B2,
  input  Ca2,
  input  G3_2,
  input  P3_2,
  input  A3,
  input  B3,
  input  Ca3,
  input  G3_3,
  output Ca1_2,
  output C0,
  output Ca2_2,
  output S0,
  output S1,
  output C1,
  output Ca3_2,
  output Ca4,
  output C2,
  output C3,
  output C4
);

  wire and_1_out, CinP0_out, CinP0P1_out, CinP0P1P2_out, not_1_out, not_2_out, not_3_out, not_4_out,
       P1G0_out, P2G1_out, P2P1G0_out, P3G2_out, P3P2G1_out, P3P2P1G0_out, P3P2P1P0Cin_out, xor_1_out,
       xor_2_out, xor_3_out, xor_4_out, xor_5_out, xor_6_out, xor_7_out, xor_8_out;

  and A0B0 (G0, A0, B0);
  or or_1 (P0_2, A0, B0);
  not not_1 (not_1_out, A0);
  xor xor_1 (xor_1_out, B0, A0);
  and A1B1 (G1_2, A1, B1);
  or or_2 (P1_2, A1, B1);
  not not_2 (not_2_out, A1);
  xor xor_2 (xor_2_out, B1, A1);
  and A2B2 (G2_2, A2, B2);
  or or_3 (P2_2, A2, B2);
  not not_3 (not_3_out, A2);
  xor xor_3 (xor_3_out, B2, A2);
  and A3B3 (G3_2, A3, B3);
  or or_4 (P3_2, A3, B3);
  not not_4 (not_4_out, A3);
  xor xor_4 (xor_4_out, B3, A3);
  xor xor_5 (xor_5_out, xor_1_out, CIN_2);
  xor xor_6 (xor_6_out, xor_2_out, Ca1);
  xor xor_7 (xor_7_out, xor_3_out, Ca2);
  xor xor_8 (xor_8_out, xor_4_out, Ca3);
  and and_1 (and_1_out, xor_4_out, Ca3);
  Multiplexer #(.select(2), .enable("false")) multiplexer_1 (
    .in0(G0), .in1(P0_2), .in2(not_1_out), .in3(xor_5_out), .out(C0), .sel({S1, S0}));
  Multiplexer #(.select(2), .enable("false")) multiplexer_2 (
    .in0(G1_2), .in1(P1_2), .in2(not_2_out), .in3(xor_6_out), .out(C1), .sel({S1, S0}));
  Multiplexer #(.select(2), .enable("false")) multiplexer_3 (
    .in0(G2_2), .in1(P2_2), .in2(not_3_out), .in3(xor_7_out), .out(C2), .sel({S1, S0}));
  Multiplexer #(.select(2), .enable("false")) multiplexer_4 (
    .in0(G3_2), .in1(P3_2), .in2(not_4_out), .in3(xor_8_out), .out(C3), .sel({S1, S0}));
  or or_5 (C4, and_1_out, G3_3);
  and CinP0 (CinP0_out, P0, CIN);
  and CinP0P1 (CinP0P1_out, P0, CIN, P1);
  and P1G0 (P1G0_out, G0_2, P1);
  and CinP0P1P2 (CinP0P1P2_out, CIN, P0, P1, P2);
  and P2P1G0 (P2P1G0_out, P2, P1, G0_2);
  and P2G1 (P2G1_out, P2, G1);
  and P3G2 (P3G2_out, P3, G2);
  and P3P2G1 (P3P2G1_out, P3, P2, G1);
  and P3P2P1G0 (P3P2P1G0_out, P3, P2, P1, G0_2);
  and P3P2P1P0Cin (P3P2P1P0Cin_out, P3, P2, P1, P0, CIN);
  or or_6 (Ca1_2, CinP0_out, G0_2);
  or or_7 (Ca2_2, CinP0P1_out, P1G0_out, G1);
  or or_8 (Ca3_2, CinP0P1P2_out, P2P1G0_out, P2G1_out, G2);
  or or_9 (Ca4, P3G2_out, P3P2G1_out, P3P2P1G0_out, P3P2P1P0Cin_out, G3);
endmodule
